// Logisim project Roy_Nishant.circ as structural Verilog
module main (
  input  [31:0] in_1
);

  wire [1:0] undriven;
  wire [31:0] adder_1_out;

  Adder #(.width(32)) adder_1 (.a(in_1), .b({32{1'b1}}), .out(adder_1_out));  // open: cin, cout
  Multiplexer #(.select(2), .width(32), .enable("false")) multiplexer_1 (
    .in0(adder_1_out), .sel(undriven));  // open: in1, in2, in3, out

  // Other names for the same wires on the sheet: PC[31:0] = in_1
endmodule

module Dual_Ported_Register_File (
  input  CLK,
  input  WrEN,
  input  [3:0] WrREGNO,
  input  [3:0] RdREGNO1,
  input  [3:0] RdREGNO2,
  input  [31:0] INPUT,
  output [31:0] OUT1,
  output [31:0] OUT2
);

  wire En_a0, En_a1, En_a2, En_at, En_fp, En_k0, En_ra, En_s0, En_s1, En_s2, En_sp, En_t0, En_t1, En_t2,
       En_v0;
  wire [31:0] a0, a1, a2, at, fp, k0, ra, s0, s1, s2, sp, t0, t1, t2, v0, zero;

  Decoder #(.select(4), .disabled(0)) decoder_1 (
    .out1(En_at), .out2(En_v0), .out3(En_a0), .out4(En_a1), .out5(En_a2), .out6(En_t0), .out7(En_t1),
    .out8(En_t2), .out9(En_s0), .out10(En_s1), .out11(En_s2), .out12(En_k0), .out13(En_sp), .out14(En_fp),
    .out15(En_ra), .sel(WrREGNO), .en(WrEN));  // open: out0
  Register #(.width(32)) u_zero (.D(INPUT), .en(1'b0), .Q(zero), .clk(CLK));  // open: clr
  Register #(.width(32)) u_at (.D(INPUT), .en(En_at), .Q(at), .clk(CLK));  // open: clr
  Register #(.width(32)) u_v0 (.D(INPUT), .en(En_v0), .Q(v0), .clk(CLK));  // open: clr
  Register #(.width(32)) u_a0 (.D(INPUT), .en(En_a0), .Q(a0), .clk(CLK));  // open: clr
  Register #(.width(32)) u_a1 (.D(INPUT), .en(En_a1), .Q(a1), .clk(CLK));  // open: clr
  Register #(.width(32)) u_a2 (.D(INPUT), .en(En_a2), .Q(a2), .clk(CLK));  // open: clr
  Register #(.width(32)) u_t0 (.D(INPUT), .en(En_t0), .Q(t0), .clk(CLK));  // open: clr
  Register #(.width(32)) u_t1 (.D(INPUT), .en(En_t1), .Q(t1), .clk(CLK));  // open: clr
  Multiplexer #(.select(4), .width(32), .disabled(0), .enable("false")) multiplexer_1 (
    .in0(zero), .in1(at), .in2(v0), .in3(a0), .in4(a1), .in5(a2), .in6(t0), .in7(t1), .in8(t2), .in9(s0),
    .in10(s1), .in11(s2), .in12(k0), .in13(sp), .in14(fp), .in15(ra), .out(OUT2), .sel(RdREGNO2));
  Register #(.width(32)) u_t2 (.D(INPUT), .en(En_t2), .Q(t2), .clk(CLK));  // open: clr
  Register #(.width(32)) u_s0 (.D(INPUT), .en(En_s0), .Q(s0), .clk(CLK));  // open: clr
  Register #(.width(32)) u_s1 (.D(INPUT), .en(En_s1), .Q(s1), .clk(CLK));  // open: clr
  Register #(.width(32)) u_s2 (.D(INPUT), .en(En_s2), .Q(s2), .clk(CLK));  // open: clr
  Register #(.width(32)) u_k0 (.D(INPUT), .en(En_k0), .Q(k0), .clk(CLK));  // open: clr
  Register #(.width(32)) u_sp (.D(INPUT), .en(En_sp), .Q(sp), .clk(CLK));  // open: clr
  Register #(.width(32)) u_fp (.D(INPUT), .en(En_fp), .Q(fp), .clk(CLK));  // open: clr
  Register #(.width(32)) u_ra (.D(INPUT), .en(En_ra), .Q(ra), .clk(CLK));  // open: clr
  Multiplexer #(.select(4), .width(32), .disabled(0), .enable("false")) multiplexer_2 (
    .in0(zero), .in1(at), .in2(v0), .in3(a0), .in4(a1), .in5(a2), .in6(t0), .in7(t1), .in8(t2), .in9(s0),
    .in10(s1), .in11(s2), .in12(k0), .in13(sp), .in14(fp), .in15(ra), .out(OUT1), .sel(RdREGNO1));

  // Notes on the sheet:
  //   MODIFY AT YOUR OWN RISK
endmodule

module IF_IDRR_Buffer (
  input  in_1,
  input  [31:0] in_2,
  input  [31:0] in_3,
  input  in_4,
  output [3:0] out_5,
  output [3:0] out_6,
  output [19:0] out_7,
  output [31:0] out_8,
  output [3:0] out_9,
  output [3:0] out_10
);

  wire [31:0] multiplexer_1_out, multiplexer_2_out;

  Multiplexer #(.width(32), .enable("false")) multiplexer_1 (
    .in0(in_2), .in1({32{1'b0}}), .out(multiplexer_1_out), .sel(in_1));
  Multiplexer #(.width(32), .enable("false")) multiplexer_2 (
    .in0(in_3), .in1({32{1'b0}}), .out(multiplexer_2_out), .sel(in_1));
  Register #(.width(32)) register_1 (
    .D(multiplexer_1_out), .Q({out_10, out_6, out_9, out_7[19:4], out_5}), .clk(in_4));  // open: en, clr
  Register #(.width(32)) register_2 (.D(multiplexer_2_out), .Q(in_3), .clk(in_4));  // open: en, clr

  assign out_7[3:0] = out_5;
  assign out_8 = in_3;

  // Other names for the same wires on the sheet: Offset[19:0] = {out_7[19:4], out_5}; RZ[3:0] = out_5;
  //   RY[3:0] = out_9; RX[3:0] = out_6; OP[3:0] = out_10; Clock = in_4; Flush = in_1; Instruction[31:0] = in_2;
  //   PC___1[31:0] = in_3
endmodule
